// Logisim project LC-2200-16.circ as structural Verilog: 6 circuits, main circuit Datapath
module Main (
  output [15:0] Bus
);

  wire Clock_out, Datapath_z, Microcontrol_Unit_dralu, Microcontrol_Unit_drmem, Microcontrol_Unit_droff,
       Microcontrol_Unit_drpc, Microcontrol_Unit_drreg, Microcontrol_Unit_lda, Microcontrol_Unit_ldb,
       Microcontrol_Unit_ldir, Microcontrol_Unit_ldmar, Microcontrol_Unit_ldpc, Microcontrol_Unit_ldz,
       Microcontrol_Unit_wrmem, Microcontrol_Unit_wrreg;
  wire [1:0] Microcontrol_Unit_alulo, Microcontrol_Unit_regsello;
  wire [2:0] Datapath_opcode;
  wire [3:0] Datapath_rx, Datapath_ry, Datapath_rz, multiplexer_1_out;

  Clock Clock (.out(Clock_out));
  Microcontrol_Unit Microcontrol_Unit (
    .Clock(Clock_out), .DrREG(Microcontrol_Unit_drreg), .DrMEM(Microcontrol_Unit_drmem),
    .DrALU(Microcontrol_Unit_dralu), .DrPC(Microcontrol_Unit_drpc), .DrOFF(Microcontrol_Unit_droff),
    .LdPC(Microcontrol_Unit_ldpc), .LdIR(Microcontrol_Unit_ldir), .LdMAR(Microcontrol_Unit_ldmar),
    .LdA(Microcontrol_Unit_lda), .LdB(Microcontrol_Unit_ldb), .LdZ(Microcontrol_Unit_ldz),
    .WrREG(Microcontrol_Unit_wrreg), .IR_15_13___opcode(Datapath_opcode), .WrMEM(Microcontrol_Unit_wrmem),
    .RegSelLo(Microcontrol_Unit_regsello[0]), .RegSelHi(Microcontrol_Unit_regsello[1]),
    .ALULo(Microcontrol_Unit_alulo[0]), .ALUHi(Microcontrol_Unit_alulo[1]), .Z(Datapath_z));
  Datapath Datapath (
    .Clock(Clock_out), .LdPC(Microcontrol_Unit_ldpc), .LdA(Microcontrol_Unit_lda),
    .LdB(Microcontrol_Unit_ldb), .LdMAR(Microcontrol_Unit_ldmar), .LdIR(Microcontrol_Unit_ldir),
    .DrPC(Microcontrol_Unit_drpc), .DrALU(Microcontrol_Unit_dralu), .DrREG(Microcontrol_Unit_drreg),
    .DrMEM(Microcontrol_Unit_drmem), .DrOFF(Microcontrol_Unit_droff), .LdZ(Microcontrol_Unit_ldz),
    .func(Microcontrol_Unit_alulo), .Bus(Bus), .WrREG(Microcontrol_Unit_wrreg),
    .WrMEM(Microcontrol_Unit_wrmem), .RZ(Datapath_rz), .RY(Datapath_ry), .RX(Datapath_rx),
    .regno(multiplexer_1_out), .opcode(Datapath_opcode), .Z(Datapath_z));
  Multiplexer #(.select(2), .width(4)) multiplexer_1 (
    .in0(Datapath_rx), .in1(Datapath_ry), .in2(Datapath_rz), .out(multiplexer_1_out),
    .sel(Microcontrol_Unit_regsello));  // open: in3, en
endmodule

module Datapath (
  input  Clock,
  input  [3:0] regno,
  input  LdPC,
  input  LdA,
  input  LdB,
  input  LdMAR,
  input  LdIR,
  input  WrREG,
  input  [1:0] func,
  input  WrMEM,
  input  DrPC,
  input  DrALU,
  input  DrREG,
  input  DrMEM,
  input  DrOFF,
  input  LdZ,
  output [3:0] RZ,
  output [3:0] RY,
  output [3:0] RX,
  output [2:0] opcode,
  output [15:0] Bus,
  output Z
);

  wire _0_result;
  wire [0:0] IR_q;
  wire [3:0] Reg0_regno_2;
  wire [15:0] A_q, ALU_result, B_q, bit_extender_1_out, MAR_q, PC_q, ram_1_data, ram_2_data, Reg0_dout;

  Register #(.width(16)) PC (.D(Bus), .en(LdPC), .Q(PC_q), .clk(Clock));  // open: clr
  assign Bus = DrPC ? PC_q : 16'bz;  // Controlled_Buffer controlled_buffer_1
  Zero_Detector _0 (.Input(Bus), .Result(_0_result));
  Register #(.width(1)) u_Z (.D(_0_result), .en(LdZ), .Q(Z), .clk(Clock));  // open: clr
  Register #(.width(16)) A (.D(Bus), .en(LdA), .Q(A_q), .clk(Clock));  // open: clr
  ALU ALU (.B(B_q), .A(A_q), .func(func), .Result(ALU_result));
  assign Bus = DrALU ? ALU_result : 16'bz;  // Controlled_Buffer controlled_buffer_2
  Register #(.width(16)) B (.D(Bus), .en(LdB), .Q(B_q), .clk(Clock));  // open: clr
  Reg0 Reg0 (.regno(regno), .Din(Bus), .regno_2(Reg0_regno_2), .Dout(Reg0_dout));
  assign Bus = DrREG ? ram_1_data : 16'bz;  // Controlled_Buffer controlled_buffer_3
  RAM #(.addrWidth(4), .dataWidth(16), .bus("separate")) ram_1 (
    .addr(Reg0_regno_2), .din(Reg0_dout), .data(ram_1_data), .str(WrREG), .clk(Clock));  // open: sel, ld, clr
  Register #(.width(16)) MAR (.D(Bus), .en(LdMAR), .Q(MAR_q), .clk(Clock));  // open: clr
  RAM #(.addrWidth(16), .dataWidth(16), .bus("separate")) ram_2 (
    .addr(MAR_q), .din(Bus), .data(ram_2_data), .str(WrMEM), .clk(Clock));  // open: sel, ld, clr
  assign Bus = DrMEM ? ram_2_data : 16'bz;  // Controlled_Buffer controlled_buffer_4
  Register #(.width(16)) IR (.D(Bus), .en(LdIR), .Q({opcode, RX, RY, RZ, IR_q[0]}), .clk(Clock));  // open: clr
  assign bit_extender_1_out = {{11{RZ[3]}}, {RZ, IR_q[0]}};  // Bit_Extender bit_extender_1
  assign Bus = DrOFF ? bit_extender_1_out : 16'bz;  // Controlled_Buffer controlled_buffer_5

  // Notes on the sheet:
  //   SPRING 2016
endmodule

module Microcontrol_Unit (
  input  [2:0] IR_15_13___opcode,
  input  Clock,
  input  Z,
  output DrREG,
  output DrMEM,
  output DrALU,
  output DrPC,
  output DrOFF,
  output LdPC,
  output LdIR,
  output LdMAR,
  output LdA,
  output LdB,
  output LdZ,
  output WrREG,
  output WrMEM,
  output RegSelLo,
  output RegSelHi,
  output ALULo,
  output ALUHi
);

  wire [5:0] multiplexer_1_out, register_1_q, rom_2_data, rom_3_data;
  wire [24:0] rom_1_data;

  ROM #(.addrWidth(6), .dataWidth(25)) rom_1 (
    .addr(register_1_q),
    .data({rom_1_data[24:23], ALUHi, ALULo, RegSelHi, RegSelLo, WrMEM, WrREG, LdZ, LdB, LdA, LdMAR, LdIR, LdPC, DrOFF, DrPC, DrALU, DrMEM, DrREG, rom_1_data[5:0]}));  // open: sel
  Register #(.width(6)) register_1 (.D(multiplexer_1_out), .Q(register_1_q), .clk(Clock));  // open: en, clr
  Multiplexer #(.select(2), .width(6)) multiplexer_1 (
    .in0(rom_1_data[5:0]), .in1(rom_2_data), .in2(rom_3_data), .out(multiplexer_1_out),
    .sel(rom_1_data[24:23]));  // open: in3, en
  ROM #(.addrWidth(3), .dataWidth(6)) rom_2 (.addr(IR_15_13___opcode), .data(rom_2_data));  // open: sel
  ROM #(.addrWidth(2), .dataWidth(6)) rom_3 (.addr({1'b0, Z}), .data(rom_3_data));  // open: sel

  // Notes on the sheet:
  //   Main
  //   contents of rom_1 (hex, n*v repeats v):
  //   6201 1082 e00900 84044 108045 20100 84047 88048 404109 420100 8404b 840c 20100 8404e 840f 2110 20080
  //   84052 8413 2114 40040 4056 88057 410118 1000000 421a 841b 900 a021d 840 1e
  //   Sequencer
  //   OnZ
  //   contents of rom_2 (hex, n*v repeats v):
  //   3 6 a d 11 15 1c 1e
  //   contents of rom_3 (hex, n*v repeats v):
  //   0 19
endmodule

module ALU (
  input  [15:0] B,
  input  [15:0] A,
  input  [1:0] func,
  output [15:0] Result
);

  wire [15:0] adder_1_out, adder_2_out, nand_1_out, subtractor_1_out;

  Adder #(.width(16)) adder_1 (.a(A), .b(B), .out(adder_1_out));  // open: cin, cout
  assign nand_1_out = ~(A & B);  // NAND_Gate nand_1, 16 bits wide
  Subtractor #(.width(16)) subtractor_1 (.a(A), .b(B), .out(subtractor_1_out));  // open: bin, bout
  Adder #(.width(16)) adder_2 (.a(A), .b(16'h1), .out(adder_2_out));  // open: cin, cout
  Multiplexer #(.select(2), .width(16), .enable("false")) multiplexer_1 (
    .in0(adder_1_out), .in1(nand_1_out), .in2(subtractor_1_out), .in3(adder_2_out), .out(Result), .sel(func));
endmodule

module Zero_Detector (
  input  [15:0] Input,
  output Result
);

  nor nor_1 (Result, Input[0], Input[1], Input[2], Input[3], Input[4], Input[5], Input[6], Input[7], Input[8], Input[9], Input[10], Input[11], Input[12], Input[13], Input[14], Input[15]);
endmodule

module Reg0 (
  input  [3:0] regno,
  input  [15:0] Din,
  output [3:0] regno_2,
  output [15:0] Dout
);

  wire nor_1_out, not_1_out;

  nor nor_1 (nor_1_out, regno[0], regno[1], regno[2], regno[3]);
  not not_1 (not_1_out, nor_1_out);
  assign Dout = nor_1_out ? {16{1'b0}} : 16'bz;  // Controlled_Buffer controlled_buffer_1
  assign Dout = not_1_out ? Din : 16'bz;  // Controlled_Buffer controlled_buffer_2

  assign regno_2 = regno;
endmodule
