// Logisim project chen_jesse.circ as structural Verilog: 8 circuits, main circuit main
module main (
);

  wire Clock, comparator_1_eq, comparator_2_eq, comparator_3_eq, comparator_4_gt, comparator_5_eq,
       comparator_6_eq, comparator_7_eq, comparator_9_eq, comparator_11_eq, comparator_12_eq, DBUF_CLR,
       FBUF_CLR, FBUF_EN, or_2_out, Stall, WrEN;
  wire [0:0] comparator_4_eq;
  wire [1:0] comparator_12_gt, IFSel;
  wire [3:0] EX_opcode, EX_WrREGNO, IDRR_opcode, MEM_opcode, MEM_WrREGNO, multiplexer_3_out, RdREGNO1,
       RdREGNO2, RX, RY, WB_opcode, WB_WrREGNO;
  wire [19:0] DBUF_offset_2, OFFSET;
  wire [31:0] adder_1_out, BEQ, DBUF_dbuf_pc_1_2, DPRF_IN, DPRF_OUT1, DPRF_OUT2, EBUF_ebuf_pc_1_2,
       EBUF_ebuf_wrin_2, EX_OUT, IDRR_OUT1, IDRR_OUT2, JALR, MBUF_mbuf_alu_2, MBUF_mbuf_mem_2,
       MBUF_mbuf_pc_1_2, MEM_ALU, MEM_RAM, multiplexer_1_out, multiplexer_4_out, multiplexer_5_out, PC_1,
       PC_q, rom_1_data, WrIN;

  Clock u_Clock (.out(Clock));
  Register #(.width(32)) PC (.D(multiplexer_1_out), .en(FBUF_EN), .Q(PC_q), .clk(Clock));  // open: clr
  not not_1 (FBUF_EN, Stall);
  or or_1 (FBUF_CLR, IFSel[0], IFSel[1]);
  Multiplexer #(.select(2), .width(32)) multiplexer_1 (
    .in0(adder_1_out), .in1(BEQ), .in2(JALR), .out(multiplexer_1_out), .sel(IFSel));  // open: in3, en
  Adder #(.width(32)) adder_1 (.a(32'h1), .b(PC_q), .out(adder_1_out));  // open: cin, cout
  Comparator #(.width(4)) comparator_1 (.a(EX_WrREGNO), .b(RdREGNO1), .eq(comparator_1_eq));  // open: gt, lt
  or or_2 (or_2_out, comparator_1_eq, comparator_2_eq);
  Comparator #(.width(4)) comparator_2 (.a(EX_WrREGNO), .b(RdREGNO2), .eq(comparator_2_eq));  // open: gt, lt
  Comparator #(.width(4)) comparator_3 (.a(EX_opcode), .b(4'b0011), .eq(comparator_3_eq));  // open: gt, lt
  ROM #(.addrWidth(24), .dataWidth(32)) rom_1 (.addr(PC_q[23:0]), .data(rom_1_data));  // open: sel
  and and_1 (Stall, or_2_out, comparator_3_eq);
  Multiplexer multiplexer_2 (.in0(FBUF_CLR), .in1(Stall), .out(DBUF_CLR), .sel(comparator_3_eq));  // open: en
  IF_IDRR_Buffer FBUF (
    .FBUF_PC_1(adder_1_out), .Instruction(rom_1_data), .Clear(FBUF_CLR), .Enable(FBUF_EN), .Clock(Clock),
    .FBUF_PC_1_2(PC_1), .Instruction_2({IDRR_opcode, RX, RY, OFFSET}));
  Multiplexer #(.select(3), .width(12)) multiplexer_3 (
    .in0({OFFSET[3:0], RY, RX}), .in1({OFFSET[3:0], RY, RX}), .in2({4'b0000, RY, RX}),
    .in3({4'b0000, RY, RX}), .in4({RX, RY, 4'b0000}), .in5({RX, RY, 4'b0000}), .in6({4'b0000, RX, RY}),
    .out({RdREGNO2, RdREGNO1, multiplexer_3_out}), .sel(IDRR_opcode[2:0]));  // open: in7, en
  Dual_Ported_Register_File dual_ported_register_file_1 (
    .CLK(Clock), .WrREGNO(WB_WrREGNO), .RdREGNO1(RdREGNO1), .RdREGNO2(RdREGNO2), .INPUT(DPRF_IN),
    .OUT1(DPRF_OUT1), .OUT2(DPRF_OUT2), .WrEN(WrEN));
  Forwarding_Unit Forwarding_Unit (
    .RdREGNO1(RdREGNO1), .EX_WrREGNO(EX_WrREGNO), .EX_opcode(EX_opcode), .MEM_WrREGNO(MEM_WrREGNO),
    .MEM_opcode(MEM_opcode), .WB_WrREGNO(WB_WrREGNO), .WB_opcode(WB_opcode), .RdREGNO2(RdREGNO2),
    .IDRR_OUT1(IDRR_OUT1), .IDRR_OUT2(IDRR_OUT2), .DPRF_OUT1(DPRF_OUT1), .DPRF_OUT2(DPRF_OUT2),
    .EX_OUT(EX_OUT), .MEM_ALU(MEM_ALU), .MEM_RAM(MEM_RAM), .WB_OUT(DPRF_IN));
  IDRR_EX_Buffer DBUF (
    .DBUF_PC_1(PC_1), .DBUF_WrREGNO(multiplexer_3_out), .DBUF_A(IDRR_OUT1), .DBUF_B(IDRR_OUT2),
    .OFFSET(OFFSET), .DBUF_opcode(IDRR_opcode), .Clear(DBUF_CLR), .Clock(Clock),
    .DBUF_PC_1_2(DBUF_dbuf_pc_1_2), .DBUF_WrREGNO_2(EX_WrREGNO), .DBUF_A_2(JALR), .DBUF_B_2(WrIN),
    .OFFSET_2(DBUF_offset_2), .DBUF_opcode_2(EX_opcode));
  Comparator #(.width(4)) comparator_4 (
    .a(EX_opcode), .b(4'b0001), .gt(comparator_4_gt), .eq(comparator_4_eq[0]));  // open: lt
  Adder #(.width(32)) adder_2 (.a(DBUF_dbuf_pc_1_2), .b(multiplexer_5_out), .out(BEQ));  // open: cin, cout
  Multiplexer #(.width(32)) multiplexer_4 (
    .in0(WrIN), .in1(multiplexer_5_out), .out(multiplexer_4_out), .sel(comparator_4_gt));  // open: en
  Comparator #(.width(1)) comparator_5 (.a(DBUF_offset_2[19]), .b(1'b1), .eq(comparator_5_eq));  // open: gt, lt
  Multiplexer #(.width(32)) multiplexer_5 (
    .in0({{12{1'b0}}, DBUF_offset_2}), .in1({{12{1'b1}}, DBUF_offset_2}), .out(multiplexer_5_out),
    .sel(comparator_5_eq));  // open: en
  Comparator #(.width(4)) comparator_6 (.a(EX_opcode), .b(4'b0101), .eq(comparator_6_eq));  // open: gt, lt
  Comparator #(.width(32)) comparator_7 (.a(JALR), .b(WrIN), .eq(comparator_7_eq));  // open: gt, lt
  Comparator #(.width(4)) comparator_8 (.a(EX_opcode), .b(4'b0110), .eq(IFSel[1]));  // open: gt, lt
  ALU alu_1 (.FUNC({1'b0, comparator_4_eq[0]}), .A(JALR), .B(multiplexer_4_out), .OUT(EX_OUT));
  and and_2 (IFSel[0], comparator_6_eq, comparator_7_eq);
  EX_MEM_Buffer EBUF (
    .EBUF_WrREGNO(EX_WrREGNO), .EBUF_PC_1(DBUF_dbuf_pc_1_2), .EBUF_WrIN(WrIN), .EBUF_ALU(EX_OUT),
    .EBUF_opcode(EX_opcode), .Clock(Clock), .EBUF_WrREGNO_2(MEM_WrREGNO), .EBUF_PC_1_2(EBUF_ebuf_pc_1_2),
    .EBUF_WrIN_2(EBUF_ebuf_wrin_2), .EBUF_ALU_2(MEM_ALU), .EBUF_opcode_2(MEM_opcode));
  Comparator #(.width(4), .mode("unsigned")) comparator_9 (
    .a(MEM_opcode), .b(4'b0100), .eq(comparator_9_eq));  // open: gt, lt
  RAM #(.addrWidth(24), .dataWidth(32), .bus("separate")) ram_1 (
    .addr(MEM_ALU[23:0]), .din(EBUF_ebuf_wrin_2), .data(MEM_RAM), .str(comparator_9_eq), .clk(Clock));  // open: sel, ld, clr
  MEM_WB_Buffer MBUF (
    .MBUF_PC_1(EBUF_ebuf_pc_1_2), .MBUF_WrREGNO(MEM_WrREGNO), .MBUF_MEM(MEM_RAM), .MBUF_opcode(MEM_opcode),
    .Clock(Clock), .MBUF_PC_1_2(MBUF_mbuf_pc_1_2), .MBUF_WrREGNO_2(WB_WrREGNO), .MBUF_MEM_2(MBUF_mbuf_mem_2),
    .MBUF_opcode_2(WB_opcode), .MBUF_ALU(MEM_ALU), .MBUF_ALU_2(MBUF_mbuf_alu_2));
  Comparator #(.width(4)) comparator_10 (.a(WB_opcode), .b(4'b0011), .eq(comparator_12_gt[1]));  // open: gt, lt
  Comparator #(.width(4)) comparator_11 (.a(WB_opcode), .b(4'b0100), .eq(comparator_11_eq));  // open: gt, lt
  Comparator #(.width(4)) comparator_12 (
    .a(WB_opcode), .b(4'b0101), .gt(comparator_12_gt[0]), .eq(comparator_12_eq));  // open: lt
  Multiplexer #(.select(2), .width(32)) multiplexer_6 (
    .in0(MBUF_mbuf_alu_2), .in1(MBUF_mbuf_pc_1_2), .in2(MBUF_mbuf_mem_2), .out(DPRF_IN),
    .sel(comparator_12_gt));  // open: in3, en
  and and_3 (WrEN, ~comparator_11_eq, ~comparator_12_eq);  // AND_Gate

  // Other names for the same wires on the sheet: RZ[3:0] = OFFSET[3:0]; WB_OUT[31:0] = DPRF_IN

  // Notes on the sheet:
  //   contents of rom_1 (hex, n*v repeats v):
  //   2300002f 3dd00000 21000007 23000008 61f00000 21000026 61000000 ed00000 2dd00004 4fe00000 8300000
  //   233fffff 43e00001 293fffff 49e00002 2a000001 5800000c 58a0000f 61f00000 3fe00000 42e00003 33e00002
  //   61f00000 3fe00000 39e00003 2900002 2ddffffc 2eeffffc 6f000000 22000000 2ddffffc 2eeffffc 6f000000
  //   22000001 2ddffffc 2eeffffc 6f000000 4000
endmodule

module Dual_Ported_Register_File (
  input  CLK,
  input  WrEN,
  input  [3:0] WrREGNO,
  input  [3:0] RdREGNO1,
  input  [3:0] RdREGNO2,
  input  [31:0] INPUT,
  output [31:0] OUT1,
  output [31:0] OUT2
);

  wire En_a0, En_a1, En_a2, En_a3, En_a4, En_at, En_fp, En_k0, En_ra, En_s0, En_s1, En_s2, En_s3, En_sp,
       En_v0;
  wire [31:0] a0, a1, a2, a3, a4, at, fp, k0, ra, s0, s1, s2, s3, sp, v0, zero;

  Decoder #(.select(4), .disabled(0)) decoder_1 (
    .out1(En_at), .out2(En_v0), .out3(En_a0), .out4(En_a1), .out5(En_a2), .out6(En_a3), .out7(En_a4),
    .out8(En_s0), .out9(En_s1), .out10(En_s2), .out11(En_s3), .out12(En_k0), .out13(En_sp), .out14(En_fp),
    .out15(En_ra), .sel(WrREGNO), .en(WrEN));  // open: out0
  Register #(.width(32)) u_zero (.D(INPUT), .en(1'b0), .Q(zero), .clk(CLK));  // open: clr
  Register #(.width(32)) u_at (.D(INPUT), .en(En_at), .Q(at), .clk(CLK));  // open: clr
  Register #(.width(32)) u_v0 (.D(INPUT), .en(En_v0), .Q(v0), .clk(CLK));  // open: clr
  Register #(.width(32)) u_a0 (.D(INPUT), .en(En_a0), .Q(a0), .clk(CLK));  // open: clr
  Register #(.width(32)) u_a1 (.D(INPUT), .en(En_a1), .Q(a1), .clk(CLK));  // open: clr
  Register #(.width(32)) u_a2 (.D(INPUT), .en(En_a2), .Q(a2), .clk(CLK));  // open: clr
  Register #(.width(32)) u_a3 (.D(INPUT), .en(En_a3), .Q(a3), .clk(CLK));  // open: clr
  Register #(.width(32)) u_a4 (.D(INPUT), .en(En_a4), .Q(a4), .clk(CLK));  // open: clr
  Multiplexer #(.select(4), .width(32), .disabled(0), .enable("false")) multiplexer_1 (
    .in0(zero), .in1(at), .in2(v0), .in3(a0), .in4(a1), .in5(a2), .in6(a3), .in7(a4), .in8(s0), .in9(s1),
    .in10(s2), .in11(s3), .in12(k0), .in13(sp), .in14(fp), .in15(ra), .out(OUT2), .sel(RdREGNO2));
  Register #(.width(32)) u_s0 (.D(INPUT), .en(En_s0), .Q(s0), .clk(CLK));  // open: clr
  Register #(.width(32)) u_s1 (.D(INPUT), .en(En_s1), .Q(s1), .clk(CLK));  // open: clr
  Register #(.width(32)) u_s2 (.D(INPUT), .en(En_s2), .Q(s2), .clk(CLK));  // open: clr
  Register #(.width(32)) u_s3 (.D(INPUT), .en(En_s3), .Q(s3), .clk(CLK));  // open: clr
  Register #(.width(32)) u_k0 (.D(INPUT), .en(En_k0), .Q(k0), .clk(CLK));  // open: clr
  Register #(.width(32)) u_sp (.D(INPUT), .en(En_sp), .Q(sp), .clk(CLK));  // open: clr
  Register #(.width(32)) u_fp (.D(INPUT), .en(En_fp), .Q(fp), .clk(CLK));  // open: clr
  Register #(.width(32)) u_ra (.D(INPUT), .en(En_ra), .Q(ra), .clk(CLK));  // open: clr
  Multiplexer #(.select(4), .width(32), .disabled(0), .enable("false")) multiplexer_2 (
    .in0(zero), .in1(at), .in2(v0), .in3(a0), .in4(a1), .in5(a2), .in6(a3), .in7(a4), .in8(s0), .in9(s1),
    .in10(s2), .in11(s3), .in12(k0), .in13(sp), .in14(fp), .in15(ra), .out(OUT1), .sel(RdREGNO1));

  // Notes on the sheet:
  //   MODIFY AT YOUR OWN RISK
endmodule

module IF_IDRR_Buffer (
  input  [31:0] FBUF_PC_1,
  input  [31:0] Instruction,
  input  Clear,
  input  Enable,
  input  Clock,
  output [31:0] FBUF_PC_1_2,
  output [31:0] Instruction_2
);

  wire [31:0] multiplexer_1_out, multiplexer_2_out;

  Multiplexer #(.width(32)) multiplexer_1 (
    .in0(FBUF_PC_1), .in1({32{1'b0}}), .out(multiplexer_1_out), .sel(Clear));  // open: en
  Multiplexer #(.width(32)) multiplexer_2 (
    .in0(Instruction), .in1({32{1'b0}}), .out(multiplexer_2_out), .sel(Clear));  // open: en
  Register #(.width(32)) u_FBUF_PC_1 (.D(multiplexer_1_out), .en(Enable), .Q(FBUF_PC_1_2), .clk(Clock));  // open: clr
  Register #(.width(32)) u_Instruction (
    .D(multiplexer_2_out), .en(Enable), .Q(Instruction_2), .clk(Clock));  // open: clr
endmodule

module IDRR_EX_Buffer (
  input  [31:0] DBUF_PC_1,
  input  [3:0] DBUF_WrREGNO,
  input  [31:0] DBUF_A,
  input  [31:0] DBUF_B,
  input  [19:0] OFFSET,
  input  [3:0] DBUF_opcode,
  input  Clear,
  input  Clock,
  output [31:0] DBUF_PC_1_2,
  output [3:0] DBUF_WrREGNO_2,
  output [31:0] DBUF_A_2,
  output [31:0] DBUF_B_2,
  output [19:0] OFFSET_2,
  output [3:0] DBUF_opcode_2
);

  wire [3:0] multiplexer_2_out, multiplexer_6_out;
  wire [19:0] multiplexer_5_out;
  wire [31:0] multiplexer_1_out, multiplexer_3_out, multiplexer_4_out;

  Multiplexer #(.width(32)) multiplexer_1 (
    .in0(DBUF_PC_1), .in1({32{1'b0}}), .out(multiplexer_1_out), .sel(Clear));  // open: en
  Register #(.width(32)) u_DBUF_PC_1 (.D(multiplexer_1_out), .Q(DBUF_PC_1_2), .clk(Clock));  // open: en, clr
  Multiplexer #(.width(4)) multiplexer_2 (
    .in0(DBUF_WrREGNO), .in1(4'b0000), .out(multiplexer_2_out), .sel(Clear));  // open: en
  Register #(.width(4)) u_DBUF_WrREGNO (.D(multiplexer_2_out), .Q(DBUF_WrREGNO_2), .clk(Clock));  // open: en, clr
  Register #(.width(32)) u_DBUF_A (.D(multiplexer_3_out), .Q(DBUF_A_2), .clk(Clock));  // open: en, clr
  Multiplexer #(.width(32)) multiplexer_3 (
    .in0(DBUF_A), .in1({32{1'b0}}), .out(multiplexer_3_out), .sel(Clear));  // open: en
  Multiplexer #(.width(32)) multiplexer_4 (
    .in0(DBUF_B), .in1({32{1'b0}}), .out(multiplexer_4_out), .sel(Clear));  // open: en
  Register #(.width(32)) u_DBUF_B (.D(multiplexer_4_out), .Q(DBUF_B_2), .clk(Clock));  // open: en, clr
  Multiplexer #(.width(20)) multiplexer_5 (
    .in0(OFFSET), .in1({20{1'b0}}), .out(multiplexer_5_out), .sel(Clear));  // open: en
  Register #(.width(20)) u_OFFSET (.D(multiplexer_5_out), .Q(OFFSET_2), .clk(Clock));  // open: en, clr
  Multiplexer #(.width(4)) multiplexer_6 (
    .in0(DBUF_opcode), .in1(4'b0000), .out(multiplexer_6_out), .sel(Clear));  // open: en
  Register #(.width(4)) u_DBUF_opcode (.D(multiplexer_6_out), .Q(DBUF_opcode_2), .clk(Clock));  // open: en, clr
endmodule

module EX_MEM_Buffer (
  input  [3:0] EBUF_WrREGNO,
  input  [31:0] EBUF_PC_1,
  input  [31:0] EBUF_WrIN,
  input  [31:0] EBUF_ALU,
  input  [3:0] EBUF_opcode,
  input  Clock,
  output [3:0] EBUF_WrREGNO_2,
  output [31:0] EBUF_PC_1_2,
  output [31:0] EBUF_WrIN_2,
  output [31:0] EBUF_ALU_2,
  output [3:0] EBUF_opcode_2
);

  Register #(.width(4)) u_EBUF_WrREGNO (.D(EBUF_WrREGNO), .Q(EBUF_WrREGNO_2), .clk(Clock));  // open: en, clr
  Register #(.width(32)) u_EBUF_PC_1 (.D(EBUF_PC_1), .Q(EBUF_PC_1_2), .clk(Clock));  // open: en, clr
  Register #(.width(32)) u_EBUF_WrIN (.D(EBUF_WrIN), .Q(EBUF_WrIN_2), .clk(Clock));  // open: en, clr
  Register #(.width(32)) u_EBUF_ALU (.D(EBUF_ALU), .Q(EBUF_ALU_2), .clk(Clock));  // open: en, clr
  Register #(.width(4)) u_EBUF_opcode (.D(EBUF_opcode), .Q(EBUF_opcode_2), .clk(Clock));  // open: en, clr
endmodule

module MEM_WB_Buffer (
  input  [31:0] MBUF_PC_1,
  input  [3:0] MBUF_WrREGNO,
  input  [31:0] MBUF_ALU,
  input  [31:0] MBUF_MEM,
  input  [3:0] MBUF_opcode,
  input  Clock,
  output [31:0] MBUF_PC_1_2,
  output [3:0] MBUF_WrREGNO_2,
  output [31:0] MBUF_ALU_2,
  output [31:0] MBUF_MEM_2,
  output [3:0] MBUF_opcode_2
);

  Register #(.width(32)) u_MBUF_PC_1 (.D(MBUF_PC_1), .Q(MBUF_PC_1_2), .clk(Clock));  // open: en, clr
  Register #(.width(4)) u_MBUF_WrREGNO (.D(MBUF_WrREGNO), .Q(MBUF_WrREGNO_2), .clk(Clock));  // open: en, clr
  Register #(.width(32)) u_MBUF_ALU (.D(MBUF_ALU), .Q(MBUF_ALU_2), .clk(Clock));  // open: en, clr
  Register #(.width(32)) u_MBUF_MEM (.D(MBUF_MEM), .Q(MBUF_MEM_2), .clk(Clock));  // open: en, clr
  Register #(.width(4)) u_MBUF_opcode (.D(MBUF_opcode), .Q(MBUF_opcode_2), .clk(Clock));  // open: en, clr
endmodule

module ALU (
  input  [1:0] FUNC,
  input  [31:0] A,
  input  [31:0] B,
  output [31:0] OUT
);

  wire [31:0] adder_1_out, adder_2_out, nand_1_out, subtractor_1_out;

  Adder #(.width(32)) adder_1 (.a(A), .b(B), .out(adder_1_out), .cin(1'b0));  // open: cout
  assign nand_1_out = ~(A & B);  // NAND_Gate nand_1, 32 bits wide
  Subtractor #(.width(32)) subtractor_1 (.a(A), .b(B), .out(subtractor_1_out), .bin(1'b0));  // open: bout
  Adder #(.width(32)) adder_2 (.a(A), .b({32{1'b0}}), .out(adder_2_out), .cin(1'b1));  // open: cout
  Multiplexer #(.select(2), .width(32), .disabled(0), .enable("false")) multiplexer_1 (
    .in0(adder_1_out), .in1(nand_1_out), .in2(subtractor_1_out), .in3(adder_2_out), .out(OUT), .sel(FUNC));

  // Notes on the sheet:
  //   MODIFY AT YOUR OWN RISK
endmodule

module Forwarding_Unit (
  input  [31:0] DPRF_OUT1,
  input  [31:0] DPRF_OUT2,
  input  [31:0] EX_OUT,
  input  [31:0] MEM_ALU,
  input  [31:0] MEM_RAM,
  input  [31:0] WB_OUT,
  input  [3:0] RdREGNO1,
  input  [3:0] EX_WrREGNO,
  input  [3:0] EX_opcode,
  input  [3:0] MEM_WrREGNO,
  input  [3:0] MEM_opcode,
  input  [3:0] WB_WrREGNO,
  input  [3:0] WB_opcode,
  input  [3:0] RdREGNO2,
  output [31:0] IDRR_OUT1,
  output [31:0] IDRR_OUT2
);

  wire comparator_2_eq, comparator_3_eq, comparator_4_eq, comparator_5_eq, comparator_6_eq, comparator_7_eq,
       comparator_8_lt, comparator_9_eq, comparator_10_lt, comparator_11_eq, comparator_12_lt,
       comparator_13_eq, LW, or_1_out, or_2_out, or_3_out;
  wire [2:0] and_1_out, and_2_out;
  wire [31:0] MEM_OUT;

  Comparator #(.width(4)) comparator_1 (.a(MEM_opcode), .b(4'b0011), .eq(LW));  // open: gt, lt
  Comparator #(.width(4)) comparator_2 (.a(RdREGNO1), .b(EX_WrREGNO), .eq(comparator_2_eq));  // open: gt, lt
  Comparator #(.width(4)) comparator_3 (.a(RdREGNO1), .b(MEM_WrREGNO), .eq(comparator_3_eq));  // open: gt, lt
  Comparator #(.width(4)) comparator_4 (.a(RdREGNO1), .b(WB_WrREGNO), .eq(comparator_4_eq));  // open: gt, lt
  Comparator #(.width(4)) comparator_5 (.a(RdREGNO2), .b(EX_WrREGNO), .eq(comparator_5_eq));  // open: gt, lt
  Comparator #(.width(4)) comparator_6 (.a(RdREGNO2), .b(MEM_WrREGNO), .eq(comparator_6_eq));  // open: gt, lt
  Comparator #(.width(4)) comparator_7 (.a(RdREGNO2), .b(WB_WrREGNO), .eq(comparator_7_eq));  // open: gt, lt
  Comparator #(.width(4)) comparator_8 (.a(EX_opcode), .b(4'b0100), .lt(comparator_8_lt));  // open: gt, eq
  Comparator #(.width(4)) comparator_9 (.a(EX_opcode), .b(4'b0110), .eq(comparator_9_eq));  // open: gt, lt
  Comparator #(.width(4)) comparator_10 (.a(MEM_opcode), .b(4'b0100), .lt(comparator_10_lt));  // open: gt, eq
  Comparator #(.width(4)) comparator_11 (.a(MEM_opcode), .b(4'b0110), .eq(comparator_11_eq));  // open: gt, lt
  Comparator #(.width(4)) comparator_12 (.a(WB_opcode), .b(4'b0100), .lt(comparator_12_lt));  // open: gt, eq
  Comparator #(.width(4)) comparator_13 (.a(WB_opcode), .b(4'b0110), .eq(comparator_13_eq));  // open: gt, lt
  or or_1 (or_1_out, comparator_8_lt, comparator_9_eq);
  or or_2 (or_2_out, comparator_10_lt, comparator_11_eq);
  or or_3 (or_3_out, comparator_12_lt, comparator_13_eq);
  and and_1 (and_1_out[0], comparator_2_eq, or_1_out);
  and and_2 (and_2_out[0], or_1_out, comparator_5_eq);
  and and_3 (and_1_out[1], comparator_3_eq, or_2_out);
  and and_4 (and_2_out[1], or_2_out, comparator_6_eq);
  and and_5 (and_1_out[2], comparator_4_eq, or_3_out);
  and and_6 (and_2_out[2], or_3_out, comparator_7_eq);
  Multiplexer #(.width(32)) multiplexer_1 (.in0(MEM_ALU), .in1(MEM_RAM), .out(MEM_OUT), .sel(LW));  // open: en
  Multiplexer #(.select(3), .width(32)) multiplexer_2 (
    .in0(DPRF_OUT1), .in1(EX_OUT), .in2(MEM_OUT), .in3(EX_OUT), .in4(WB_OUT), .in5(EX_OUT), .in6(MEM_OUT),
    .in7(EX_OUT), .out(IDRR_OUT1), .sel(and_1_out));  // open: en
  Multiplexer #(.select(3), .width(32)) multiplexer_3 (
    .in0(DPRF_OUT2), .in1(EX_OUT), .in2(MEM_OUT), .in3(EX_OUT), .in4(WB_OUT), .in5(EX_OUT), .in6(MEM_OUT),
    .in7(EX_OUT), .out(IDRR_OUT2), .sel(and_2_out));  // open: en

  // Notes on the sheet:
  //   EX
  //   MEM
  //   WB
endmodule
